# Fritzing sketch SimonSays (saved by Fritzing 0.9.3b)
breadboards: 1

parts:
  LED1 = LED - 5mm [color="Red (633nm)" package="5 mm [THT]"]
  R1 = Resistor [tolerance=±5% resistance=330 package=THT]
  J1 = Piezo Speaker
  Adafruit_Atmega32u1 = Adafruit Atmega32u4 Breakout Board [part_number="Atmega 32u4"]
  S1 = Pushbutton [package="[THT]"]
  R2 = Resistor [tolerance=±5% resistance=10k package=THT]

nets:
  N1: LED1.cathode, J1.pin1, Adafruit_Atmega32u1.GND, R2.Pin_0
  N2: LED1.anode, R1.Pin_0
  N3: R1.Pin_1, Adafruit_Atmega32u1.B3, S1.Pin_3, S1.Pin_4, R2.Pin_1
  N4: Adafruit_Atmega32u1.5V, S1.Pin_1, S1.Pin_2
