# Fritzing sketch SimonSays (saved by Fritzing 0.9.3b)
breadboards: 1

parts:
  LED1 = LED - 5mm [color="Red (633nm)" package="5 mm [THT]"]
  R1 = Resistor [tolerance=±5% resistance=330 package=THT]
  J1 = Piezo Speaker
  S1 = Pushbutton [package="[THT]"]
  R2 = Resistor [tolerance=±5% resistance=10k package=THT]
  LED2 = LED - 5mm [color="Orange (620nm)" package="5 mm [THT]"]
  R3 = Resistor [tolerance=±5% resistance=330 package=THT]
  S2 = Pushbutton [package="[THT]"]
  R4 = Resistor [tolerance=±5% resistance=10k package=THT]
  LED3 = LED - 5mm [color="Green (555nm)" package="5 mm [THT]"]
  R5 = Resistor [tolerance=±5% resistance=330 package=THT]
  S3 = Pushbutton [package="[THT]"]
  R6 = Resistor [tolerance=±5% resistance=10k package=THT]
  LED4 = LED - 5mm [color="Blue (430nm)" package="5 mm [THT]"]
  R7 = Resistor [tolerance=±5% resistance=330 package=THT]
  S4 = Pushbutton [package="[THT]"]
  R8 = Resistor [tolerance=±5% resistance=10k package=THT]
  Part1 = Arduino Uno (Rev3)

nets:
  N1: LED1.cathode, J1.pin1, R2.Pin_0, LED2.cathode, R4.Pin_0, LED3.cathode, R6.Pin_0, LED4.cathode, R8.Pin_0, Part1.GND
  N2: LED1.anode, R1.Pin_0
  N3: R1.Pin_1, S1.Pin_3, S1.Pin_4, R2.Pin_1, Part1.D13/SCK
  N4: J1.pin2, Part1.D5_PWM
  N5: S1.Pin_1, S1.Pin_2, S2.Pin_1, S2.Pin_2, S3.Pin_1, S3.Pin_2, S4.Pin_1, S4.Pin_2, Part1.3V3
  N6: LED2.anode, R3.Pin_0
  N7: R3.Pin_1, S2.Pin_3, S2.Pin_4, R4.Pin_1, Part1.D10_PWM/SS
  N8: LED3.anode, R5.Pin_0
  N9: R5.Pin_1, S3.Pin_3, S3.Pin_4, R6.Pin_1, Part1.D8
  N10: LED4.anode, R7.Pin_0
  N11: R7.Pin_1, S4.Pin_3, S4.Pin_4, R8.Pin_1, Part1.D2
